# Fritzing sketch coeur led (saved by Fritzing 0.9.3b)
breadboards: 1

parts:
  Composant1 = Arduino Uno (Rev3)
  LED1 = smd LED [color="Red (633nm)" package="1206 [SMD]"]
  LED2 = smd LED [color="Red (633nm)" package="1206 [SMD]"]
  LED3 = smd LED [color="Red (633nm)" package="1206 [SMD]"]
  LED4 = smd LED [color="Red (633nm)" package="1206 [SMD]"]
  LED5 = smd LED [color="Red (633nm)" package="1206 [SMD]"]
  LED6 = smd LED [color="Red (633nm)" package="1206 [SMD]"]
  LED7 = smd LED [color="Red (633nm)" package="1206 [SMD]"]
  LED8 = smd LED [color="Red (633nm)" package="1206 [SMD]"]
  LED9 = smd LED [color="Red (633nm)" package="1206 [SMD]"]
  LED10 = smd LED [color="Red (633nm)" package="1206 [SMD]"]
  R1 = Resistor [tolerance=±5% resistance=220 package="1206 [SMD]"]
  R2 = Resistor [tolerance=±5% resistance=220 package="1206 [SMD]"]
  R3 = Resistor [tolerance=±5% resistance=220 package="1206 [SMD]"]
  R5 = Resistor [tolerance=±5% resistance=220 package="1206 [SMD]"]
  R6 = Resistor [tolerance=±5% resistance=220 package="1206 [SMD]"]
  R7 = Resistor [tolerance=±5% resistance=220 package="1206 [SMD]"]
  R8 = Resistor [tolerance=±5% resistance=220 package="1206 [SMD]"]
  R9 = Resistor [tolerance=±5% resistance=220 package="1206 [SMD]"]
  R10 = Resistor [tolerance=±5% resistance=220 package="1206 [SMD]"]
  R11 = Resistor [tolerance=±5% resistance=220 package="1206 [SMD]"]

nets:
  N1: Composant1.D8, LED8.cathode
  N2: Composant1.D9_PWM, LED9.anode
  N3: Composant1.D10_PWM/SS, LED7.anode
  N4: Composant1.D11_PWM/MOSI, LED10.anode
  N5: Composant1.GND, R1.Pin_0, R2.Pin_0, R3.Pin_0, R5.Pin_0, R6.Pin_1, R7.Pin_0, R8.Pin_1, R10.Pin_1, R11.Pin_1
  N6: Composant1.D2, LED2.anode
  N7: Composant1.D3_PWM, LED6.anode
  N8: Composant1.D4, LED1.cathode
  N9: Composant1.D5_PWM, LED3.cathode
  N10: Composant1.D6_PWM, LED4.anode
  N11: Composant1.D7, LED5.cathode
  N12: LED1.anode, R3.Pin_1
  N13: LED2.cathode, R10.Pin_0
  N14: LED3.anode, R7.Pin_1
  N15: LED4.cathode, R9.Pin_1
  N16: LED5.anode, R1.Pin_1
  N17: LED6.cathode, R2.Pin_1
  N18: LED7.cathode, LED9.cathode, R6.Pin_0
  N19: LED8.anode, R11.Pin_0
  N20: LED10.cathode, R8.Pin_0
